// Logisim project FinalProjectCPU_Extra.circ as structural Verilog: 1 circuit, main circuit main
module main (
  input  CLR,
  input  Clear
);

  wire CLK, DWE, LoadCounter, SUB, WE;
  wire [1:0] AFS, RSS;
  wire [2:0] AddrA, AddrB, AddrD;
  wire [3:0] ALU_out, multiplexer_1_out, OpCode, PortA, PortB;
  wire [3:3] Data;
  wire [7:0] CounterCPU_q;
  wire [11:7] ProgramPROM_data;

  Clock u_CLK (.out(CLK));
  Counter CounterCPU (
    .clr(CLR), .load(LoadCounter), .up(1'b1), .count(1'b1), .clk(CLK), .D({1'b0, PortA[2:0], PortB}),
    .Q(CounterCPU_q));  // open: carry
  // Probe on OpCode
  ROM #(.addrWidth(4)) InstructionDecoderPROM (.addr(OpCode), .data({LoadCounter, SUB, AFS, RSS, DWE, WE}));
  // Probe on CounterCPU_q
  ROM #(.dataWidth(16)) ProgramPROM (
    .addr(CounterCPU_q),
    .data({OpCode, ProgramPROM_data[11], AddrD, ProgramPROM_data[7], AddrA, Data[3], AddrB}));
  // FinalProject_ALU CPU_ALU: pin names not known; wires that end beside it: PortA, PortB, AFS, SUB, ALU_out
  // Probe on {OpCode, ProgramPROM_data[11], AddrD, ProgramPROM_data[7], AddrA, Data[3], AddrB}
  Multiplexer #(.select(2), .width(4)) multiplexer_1 (
    .in0({Data[3], AddrB}), .in1(ALU_out), .in2(PortA), .out(multiplexer_1_out), .sel(RSS));  // open: in3
  // Probe on ALU_out
  // Probe on {Data[3], AddrB}
  // Probe on AddrB
  // Probe on AddrA
  // Probe on AddrD
  // Probe on OpCode
  // FinalProject_Register CPU_Register: pin names not known; wires that end beside it: WE, AddrD, AddrA, AddrB, multiplexer_1_out, CLK, PortA, PortB
  // Probe on PortA
  // Probe on PortB
  TTY tty_1 (.data({PortA[2:0], PortB}), .clk(CLK), .we(DWE), .clr(Clear));

  // Other names for the same wires on the sheet: Data[2:0] = AddrB

  // Notes on the sheet:
  //   contents of InstructionDecoderPROM (hex, n*v repeats v):
  //   0 1 9 2 5 15 25 35 80 6*0 75
  //   Victor Santana
  //   contents of ProgramPROM (hex, n*v repeats v):
  //   1005 1106 3001 1206 1309 3023 1406 1503 3045 1607 1704 3067 1006 110f 3001 1207 1302 3023 1402 1500
  //   3045 1605 1703 3067 1006 1101 3001 1206 130e 3023 1407 1504 3045 1606 1701 3067 1006 110e 3001 1206
  //   1301 3023 1402 1500 3045 1602 1703 3067 1003 1100 3001 1203 1305 3023 140a 1500 3054 1603 1704 3067
  //   1002 110b 3001 1203 1302 3023 1403 150d 3045 1602 1700 3067 1004 1102 7201 1003 3002 140a 1500 3054
  //   1603 1704 3067 1002 110a 3001 1203 1302 3023 1403 150d 3045 1602 1700 3067 1004 1104 7201 1303 3032
  //   100a 1100 3010 1202 130d 1403 1504 3045 1602 170d 3067 1003 1102 3001 1203 130d 3023 1402 1500 3045
  //   1602 170f 4067 1101 7201 1303 1404 7542 3035 1600 170a 3067 1003 1104 3001 1202 130d 3023 1403 1502
  //   3045 1603 170d 3067 1002 1100 3001 1204 1302 1503 f423 3054 1600 170a 3067 1000 1100 8001
endmodule
